// Logisim project BreadboardComputer.circ as structural Verilog: 6 circuits, main circuit main
module main (
);

  wire _1_out, _2_out, _3_out, _4_out, alu_3_and, alu_3_equalsflag, alu_3_overflow, ALU_out, clock_1_out,
       decoder_1_out1, decoder_1_out2, decoder_1_out3, decoder_1_out4, decoder_1_out5, decoder_1_out6,
       decoder_1_out7, decoder_1_out8, decoder_1_out9, decoder_1_out10, decoder_1_out11, decoder_1_out12,
       decoder_1_out13, decoder_1_out15, disp_1_reset, HALT_qn, IMM_out, input_1_inputflag, MEM_out, MOV_out,
       multiplexer_1_out, not_1_out, not_2_out, not_3_out, not_4_out, not_5_out, PC_carry, RESTART_out,
       STORE_2_out;
  wire [7:0] alu_3_out, controlled_buffer_1_out, disp_1_columns, disp_1_rows, displayemulator_1__0,
       displayemulator_1__1, displayemulator_1__2, displayemulator_1__3, displayemulator_1__4,
       displayemulator_1__5, displayemulator_1__6, displayemulator_1__7, PC_q, ram_1_data, registers_1_acc,
       registers_1_out, rom_1_data;

  D_Flip_Flop HALT (
    .clk(clock_1_out), .D(decoder_1_out15), .Qn(HALT_qn), .en(decoder_1_out15), .reset(RESTART_out));  // open: Q, preset
  Button RESTART (.out(RESTART_out));
  // Probe on PC_q
  Clock clock_1 (.out(clock_1_out));
  ROM rom_1 (.addr(PC_q), .data(rom_1_data), .sel(HALT_qn));
  Multiplexer #(.select(3), .disabled(0)) multiplexer_1 (
    .in0(1'b1), .in1(alu_3_equalsflag), .in2(alu_3_overflow), .in3(input_1_inputflag), .in4(not_2_out),
    .in5(not_3_out), .in6(not_4_out), .in7(not_5_out), .out(multiplexer_1_out), .sel(rom_1_data[2:0]),
    .en(decoder_1_out9));
  not not_1 (not_1_out, multiplexer_1_out);
  Counter PC (
    .load(multiplexer_1_out), .D(registers_1_acc), .count(not_1_out), .Q(PC_q), .carry(PC_carry),
    .clk(clock_1_out), .clr(RESTART_out));
  Decoder #(.select(4), .disabled(0)) decoder_1 (
    .out1(decoder_1_out1), .out2(decoder_1_out2), .out3(decoder_1_out3), .out4(decoder_1_out4),
    .out5(decoder_1_out5), .out6(decoder_1_out6), .out7(decoder_1_out7), .out8(decoder_1_out8),
    .out9(decoder_1_out9), .out10(decoder_1_out10), .out11(decoder_1_out11), .out12(decoder_1_out12),
    .out13(decoder_1_out13), .out15(decoder_1_out15), .sel(rom_1_data[7:4]), .en(HALT_qn));  // open: out0, out14
  not not_2 (not_2_out, alu_3_equalsflag);
  not not_3 (not_3_out, alu_3_overflow);
  not not_4 (not_4_out, input_1_inputflag);
  not not_5 (not_5_out, alu_3_and);
  RAM ram_1 (
    .addr(registers_1_acc), .data(ram_1_data), .sel(MEM_out), .clk(clock_1_out), .ld(decoder_1_out11));  // open: clr
  or MEM (MEM_out, decoder_1_out11, decoder_1_out10);
  or ALU (ALU_out, decoder_1_out8, decoder_1_out7, decoder_1_out6, decoder_1_out5);
  or MOV (MOV_out, decoder_1_out3, decoder_1_out4);
  assign ram_1_data = decoder_1_out10 ? registers_1_out : 8'bz;  // Controlled_Buffer STORE
  or IMM (IMM_out, decoder_1_out2, decoder_1_out1);
  assign controlled_buffer_1_out = decoder_1_out4 ? registers_1_out : 8'bz;  // Controlled_Buffer controlled_buffer_1
  assign controlled_buffer_1_out = decoder_1_out11 ? ram_1_data : 8'bz;  // Controlled_Buffer LOAD
  assign controlled_buffer_1_out = ALU_out ? alu_3_out : 8'bz;  // Controlled_Buffer ALU_2
  assign controlled_buffer_1_out = decoder_1_out3 ? registers_1_acc : 8'bz;  // Controlled_Buffer MOV_2
  or STORE_2 (STORE_2_out, IMM_out, MOV_out, decoder_1_out11, ALU_out);
  REGISTERS registers_1 (
    .CLOCK(clock_1_out), .INPUT(controlled_buffer_1_out), .ADDRESS(rom_1_data[3:0]), .ACC(registers_1_acc),
    .OUT(registers_1_out), .IMM(rom_1_data[3:0]), .LI(decoder_1_out1), .UI(decoder_1_out2),
    .STORE(STORE_2_out), .MOV(decoder_1_out3), .RESET(RESTART_out));
  // Probe on registers_1_acc
  Input input_1 (
    .Button1(_1_out), .Button2(_2_out), .Button3(_3_out), .Button4(_4_out), .SELECT(rom_1_data[3:0]),
    .CLC(clock_1_out), .INPUT(decoder_1_out13), .INPUTFLAG(input_1_inputflag));  // open: Button5, Button6
  DisplayEmulator displayemulator_1 (
    .CLOCK(clock_1_out), .ROWS(disp_1_rows), .COLUMNS(disp_1_columns), .RESET(disp_1_reset),
    ._0(displayemulator_1__0), ._1(displayemulator_1__1), ._2(displayemulator_1__2),
    ._3(displayemulator_1__3), ._4(displayemulator_1__4), ._5(displayemulator_1__5),
    ._6(displayemulator_1__6), ._7(displayemulator_1__7));
  DotMatrix #(.matrixcols(8), .matrixrows(8)) dotmatrix_1 (
    .col0(displayemulator_1__0), .col1(displayemulator_1__1), .col2(displayemulator_1__2),
    .col3(displayemulator_1__3), .col4(displayemulator_1__4), .col5(displayemulator_1__5),
    .col6(displayemulator_1__6), .col7(displayemulator_1__7));
  DISP disp_1 (
    .DATA(registers_1_acc), .OTHER(registers_1_out), .DISP(decoder_1_out12), .CLOCK(clock_1_out),
    .ROWS(disp_1_rows), .COLUMNS(disp_1_columns), .RESET(disp_1_reset));
  ALU alu_3 (
    .SUBTRACT(decoder_1_out6), .ACC(registers_1_acc), .Data2(registers_1_out), .EQUALSFLAG(alu_3_equalsflag),
    .OVERFLOW(alu_3_overflow), .OUT(alu_3_out), .CLOCK(clock_1_out), .SHIFT(decoder_1_out8), .ALU(ALU_out),
    .AND(alu_3_and));
  Button _3 (.out(_3_out));
  Button _1 (.out(_1_out));
  Button _4 (.out(_4_out));
  Button _2 (.out(_2_out));

  // Notes on the sheet:
  //   contents of rom_1 (hex, n*v repeats v):
  //   0 11 31 11 32 11 33 14 34 13 35 13 36 d1 14 21 96 46 56 36 d2 1a 21 96 86 36 d3 11 22 96 45 55 35 d4
  //   17 22 96 85 35 1f 20 37 10 20 c7 37 45 c7 17 37 46 c7 41 c2 11 20 78 10 20 38 1d 20 91 11 20 8 38 10
  //   28 71 1c 24 94 10 20 33 11 20 71 15 25 94 11 20 33 11 20 72 17 26 94 45 71 16 26 97 11 20 34 17 26
  //   90 f0 16 20 72 19 27 94 46 71 18 27 97 10 20 34 19 27 90 f0 11 20 74 16 28 91 11 20 62 32 1a 28 90
  //   11 20 52 32 11 20 73 15 29 91 81 31 18 29 90 41 51 31 1d 20 90
  //   1 LLI
  //   2 LUI
  //   3 MOV
  //   4 MOVACC
  //   5 ADD
  //   6 SUB
  //   7 EQAL
  //   8 SHIFT
  //   9 JMP
  //   10 STORE
  //   11 LOAD
  //   12 DISP
  //   13: INPUT
  //   14 FREE
  //   15: HALT
endmodule

module ALU (
  input  SHIFT,
  input  CLOCK,
  input  ALU,
  input  SUBTRACT,
  input  [7:0] ACC,
  input  [7:0] Data2,
  output EQUALSFLAG,
  output OVERFLOW,
  output [7:0] OUT,
  output AND
);

  wire adder_1_cout, comparator_1_eq, IMM_out, or_1_out, subtractor_1_bout;
  wire [7:0] adder_1_out, and_1_out, multiplexer_1_out, subtractor_1_out;

  Comparator comparator_1 (.a(ACC), .b(Data2), .eq(comparator_1_eq));  // open: gt, lt
  Adder adder_1 (.a(ACC), .b(Data2), .out(adder_1_out), .cout(adder_1_cout));  // open: cin
  Subtractor subtractor_1 (.a(Data2), .b(ACC), .out(subtractor_1_out), .bout(subtractor_1_bout));  // open: bin
  assign and_1_out = Data2 & ACC;  // AND_Gate and_1, 8 bits wide
  Multiplexer #(.width(8), .enable("false")) multiplexer_1 (
    .in0(adder_1_out), .in1({1'b0, Data2[7:1]}), .out(multiplexer_1_out), .sel(SHIFT));
  Multiplexer #(.width(8), .enable("false")) multiplexer_2 (
    .in0(multiplexer_1_out), .in1(subtractor_1_out), .out(OUT), .sel(SUBTRACT));
  or IMM (IMM_out, and_1_out[0], and_1_out[1], and_1_out[2], and_1_out[3], and_1_out[4], and_1_out[5], and_1_out[6], and_1_out[7]);
  or or_1 (or_1_out, Data2[0], adder_1_cout);
  D_Flip_Flop d_ff_1 (.clk(CLOCK), .D(comparator_1_eq), .Q(EQUALSFLAG), .en(ALU));  // open: Qn, preset, reset
  D_Flip_Flop d_ff_2 (.clk(CLOCK), .D(or_1_out), .Q(OVERFLOW), .en(ALU));  // open: Qn, preset, reset
  D_Flip_Flop d_ff_3 (.clk(CLOCK), .D(IMM_out), .Q(AND), .en(ALU));  // open: Qn, preset, reset

  // Notes on the sheet:
  //   ON equals this can be put to ACC
  //   OVERFLOW CAN TRIGGER ON SHIFT WHEN IT SHOULDN"T
endmodule

module REGISTERS (
  input  [3:0] IMM,
  input  CLOCK,
  input  UI,
  input  STORE,
  input  RESET,
  input  LI,
  input  MOV,
  input  [3:0] ADDRESS,
  input  [7:0] INPUT,
  output [7:0] ACC,
  output [7:0] OUT
);

  wire and_1_out, decoder_1_out0, decoder_1_out1, decoder_1_out2, decoder_1_out3, decoder_1_out4,
       decoder_1_out5, decoder_1_out6, decoder_1_out7, decoder_2_out0, decoder_2_out1, decoder_2_out2,
       decoder_2_out3, decoder_2_out4, decoder_2_out5, decoder_2_out6, decoder_2_out7, not_1_out, undriven;
  wire [7:0] register_2_q, register_3_q, register_4_q, register_5_q, register_6_q, register_7_q,
       register_8_q, register_9_q, register_10_q, register_11_q, register_12_q, register_13_q, register_14_q,
       register_15_q, register_16_q;

  and and_1 (and_1_out, MOV, CLOCK);
  Decoder #(.select(3), .disabled(0)) decoder_1 (
    .out0(decoder_1_out0), .out1(decoder_1_out1), .out2(decoder_1_out2), .out3(decoder_1_out3),
    .out4(decoder_1_out4), .out5(decoder_1_out5), .out6(decoder_1_out6), .out7(decoder_1_out7),
    .sel(ADDRESS[2:0]), .en(not_1_out));
  not not_1 (not_1_out, ADDRESS[3]);
  Decoder #(.select(3), .disabled(0)) decoder_2 (
    .out0(decoder_2_out0), .out1(decoder_2_out1), .out2(decoder_2_out2), .out3(decoder_2_out3),
    .out4(decoder_2_out4), .out5(decoder_2_out5), .out6(decoder_2_out6), .out7(decoder_2_out7),
    .sel(ADDRESS[2:0]), .en(ADDRESS[3]));
  assign INPUT = UI ? {IMM, ACC[3:0]} : 8'bz;  // Controlled_Buffer controlled_buffer_1
  assign INPUT = LI ? {ACC[7:4], IMM} : 8'bz;  // Controlled_Buffer controlled_buffer_2
  Register register_1 (.D(INPUT), .en(STORE), .Q(ACC), .clk(CLOCK), .clr(RESET));
  Register register_2 (.D(INPUT), .en(decoder_1_out1), .Q(register_2_q), .clk(and_1_out));  // open: clr
  Register register_3 (.D(INPUT), .en(decoder_1_out2), .Q(register_3_q), .clk(and_1_out), .clr(undriven));
  Register register_4 (.D(INPUT), .en(decoder_1_out3), .Q(register_4_q), .clk(and_1_out));  // open: clr
  Register register_5 (.D(INPUT), .en(decoder_1_out4), .Q(register_5_q), .clk(and_1_out));  // open: clr
  Register register_6 (.D(INPUT), .en(decoder_1_out5), .Q(register_6_q), .clk(and_1_out));  // open: clr
  Register register_7 (.D(INPUT), .en(decoder_1_out6), .Q(register_7_q), .clk(and_1_out));  // open: clr
  Register register_8 (.D(INPUT), .en(decoder_1_out7), .Q(register_8_q), .clk(and_1_out));  // open: clr
  Register register_9 (.D(INPUT), .en(decoder_2_out0), .Q(register_9_q), .clk(and_1_out));  // open: clr
  Register register_10 (.D(INPUT), .en(decoder_2_out1), .Q(register_10_q), .clk(and_1_out));  // open: clr
  Register register_11 (.D(INPUT), .en(decoder_2_out2), .Q(register_11_q), .clk(and_1_out));  // open: clr
  Register register_12 (.D(INPUT), .en(decoder_2_out3), .Q(register_12_q), .clk(and_1_out));  // open: clr
  Register register_13 (.D(INPUT), .en(decoder_2_out4), .Q(register_13_q), .clk(and_1_out));  // open: clr
  Register register_14 (.D(INPUT), .en(decoder_2_out5), .Q(register_14_q), .clk(and_1_out));  // open: clr
  Register register_15 (.D(INPUT), .en(decoder_2_out6), .Q(register_15_q), .clk(and_1_out));  // open: clr
  Register register_16 (.D(INPUT), .en(decoder_2_out7), .Q(register_16_q), .clk(and_1_out));  // open: clr
  Multiplexer #(.select(3), .width(8)) multiplexer_1 (
    .in0(register_9_q), .in1(register_10_q), .in2(register_11_q), .in3(register_12_q), .in4(register_13_q),
    .in5(register_14_q), .in6(register_15_q), .in7(register_16_q), .out(OUT), .sel(ADDRESS[2:0]),
    .en(ADDRESS[3]));
  Multiplexer #(.select(3), .width(8)) multiplexer_2 (
    .in0(ACC), .in1(register_2_q), .in2(register_3_q), .in3(register_4_q), .in4(register_5_q),
    .in5(register_6_q), .in6(register_7_q), .in7(register_8_q), .out(OUT), .sel(ADDRESS[2:0]), .en(not_1_out));
endmodule

module DISP (
  input  CLOCK,
  input  [7:0] DATA,
  input  [7:0] OTHER,
  input  DISP,
  output [7:0] ROWS,
  output [7:0] COLUMNS,
  output RESET
);

  wire [2:0] register_2_q;
  wire [7:0] register_1_q;

  Register #(.trigger("falling")) register_1 (.D(DATA), .en(DISP), .Q(register_1_q), .clk(CLOCK));  // open: clr
  and u_RESET (RESET, DISP, OTHER[3]);
  Register #(.width(3), .trigger("falling")) register_2 (
    .D(OTHER[2:0]), .en(DISP), .Q(register_2_q), .clk(CLOCK));  // open: clr
  assign ROWS = register_1_q;  // Buffer DRIVER, 8 bits wide
  Decoder #(.select(3), .enable("false")) decoder_1 (
    .out0(COLUMNS[0]), .out1(COLUMNS[1]), .out2(COLUMNS[2]), .out3(COLUMNS[3]), .out4(COLUMNS[4]),
    .out5(COLUMNS[5]), .out6(COLUMNS[6]), .out7(COLUMNS[7]), .sel(register_2_q));
endmodule

module DisplayEmulator (
  input  CLOCK,
  input  [7:0] ROWS,
  input  [7:0] COLUMNS,
  input  RESET,
  output [7:0] _0,
  output [7:0] _1,
  output [7:0] _2,
  output [7:0] _3,
  output [7:0] _4,
  output [7:0] _5,
  output [7:0] _6,
  output [7:0] _7
);

  wire and_1_out;

  and and_1 (and_1_out, ~CLOCK, RESET);  // AND_Gate
  Register register_1 (.D(ROWS), .en(COLUMNS[0]), .Q(_0), .clk(CLOCK), .clr(and_1_out));
  Register register_2 (.D(ROWS), .en(COLUMNS[1]), .Q(_1), .clk(CLOCK), .clr(and_1_out));
  Register register_3 (.D(ROWS), .en(COLUMNS[2]), .Q(_2), .clk(CLOCK), .clr(and_1_out));
  Register register_4 (.D(ROWS), .en(COLUMNS[3]), .Q(_3), .clk(CLOCK), .clr(and_1_out));
  Register register_5 (.D(ROWS), .en(COLUMNS[4]), .Q(_4), .clk(CLOCK), .clr(and_1_out));
  Register register_6 (.D(ROWS), .en(COLUMNS[5]), .Q(_5), .clk(CLOCK), .clr(and_1_out));
  Register register_7 (.D(ROWS), .en(COLUMNS[6]), .Q(_6), .clk(CLOCK), .clr(and_1_out));
  Register register_8 (.D(ROWS), .en(COLUMNS[7]), .Q(_7), .clk(CLOCK), .clr(and_1_out));
endmodule

module Input (
  input  [3:0] SELECT,
  input  CLC,
  input  INPUT,
  input  Button1,
  input  Button2,
  input  Button3,
  input  Button4,
  input  Button5,
  input  Button6,
  output INPUTFLAG
);

  wire multiplexer_1_out;

  Multiplexer #(.select(4)) multiplexer_1 (
    .in0(1'b0), .in1(Button1), .in2(Button2), .in3(Button3), .in4(Button4), .in5(Button5), .in6(Button6),
    .out(multiplexer_1_out), .sel(SELECT), .en(INPUT));  // open: in7, in8, in9, in10, in11, in12, in13, in14, in15
  D_Flip_Flop d_ff_1 (.clk(CLC), .D(multiplexer_1_out), .Q(INPUTFLAG), .en(INPUT));  // open: Qn, preset, reset
endmodule
