// Logisim project BreadboardComputer.circ as structural Verilog: 7 circuits, main circuit main
module main (
);

  wire clock_1_out, undriven_2;
  wire [14:0] undriven;

  DisplayEmulator displayemulator_1 ();  // open: CLOCK, ROWS, COLUMNS, RESET, _0, _1, _2, _3, _4, _5, _6, _7
  DISP disp_1 ();  // open: DATA, OTHER, DISP, CLOCK, ROWS, COLUMNS, RESET
  ROM #(.addrWidth(15)) rom_1 (.addr(undriven));  // open: data, sel
  Input input_1 ();  // open: Button1, Button2, Button3, Button4, Button5, Button6, SELECT, CLC, INPUT, INPUTFLAG
  Clock clock_1 (.out(clock_1_out));
  Counter #(.width(15), .max('h7fff)) counter_1 (
    .load(undriven_2), .D(undriven), .count(clock_1_out));  // open: Q, carry, clk, clr
  REGISTERS registers_1 ();  // open: CLOCK, INPUT, ADDRESS, ACC, OUT, IMM, LI, UI, STORE, MOV, RESET
  ALU alu_1 ();  // open: SUBTRACT, ACC, Data2, EQUALSFLAG, OVERFLOW, OUT, CLOCK, SHIFT, ALU, AND
endmodule

module ALU (
  input  SHIFT,
  input  CLOCK,
  input  ALU,
  input  SUBTRACT,
  input  [7:0] ACC,
  input  [7:0] Data2,
  output EQUALSFLAG,
  output OVERFLOW,
  output [7:0] OUT,
  output AND
);

  wire adder_1_cout, comparator_1_eq, IMM_out, or_1_out, subtractor_1_bout;
  wire [7:0] adder_1_out, and_1_out, multiplexer_1_out, subtractor_1_out;

  Comparator comparator_1 (.a(ACC), .b(Data2), .eq(comparator_1_eq));  // open: gt, lt
  Adder adder_1 (.a(ACC), .b(Data2), .out(adder_1_out), .cout(adder_1_cout));  // open: cin
  Subtractor subtractor_1 (.a(Data2), .b(ACC), .out(subtractor_1_out), .bout(subtractor_1_bout));  // open: bin
  assign and_1_out = Data2 & ACC;  // AND_Gate and_1, 8 bits wide
  Multiplexer #(.width(8), .enable("false")) multiplexer_1 (
    .in0(adder_1_out), .in1({1'b0, Data2[7:1]}), .out(multiplexer_1_out), .sel(SHIFT));
  Multiplexer #(.width(8), .enable("false")) multiplexer_2 (
    .in0(multiplexer_1_out), .in1(subtractor_1_out), .out(OUT), .sel(SUBTRACT));
  or IMM (IMM_out, and_1_out[0], and_1_out[1], and_1_out[2], and_1_out[3], and_1_out[4], and_1_out[5], and_1_out[6], and_1_out[7]);
  or or_1 (or_1_out, Data2[0], adder_1_cout);
  D_Flip_Flop d_ff_1 (.clk(CLOCK), .D(comparator_1_eq), .Q(EQUALSFLAG), .en(ALU));  // open: Qn, preset, reset
  D_Flip_Flop d_ff_2 (.clk(CLOCK), .D(or_1_out), .Q(OVERFLOW), .en(ALU));  // open: Qn, preset, reset
  D_Flip_Flop d_ff_3 (.clk(CLOCK), .D(IMM_out), .Q(AND), .en(ALU));  // open: Qn, preset, reset

  // Notes on the sheet:
  //   ON equals this can be put to ACC
  //   OVERFLOW CAN TRIGGER ON SHIFT WHEN IT SHOULDN"T
endmodule

module REGISTERS (
  input  [3:0] IMM,
  input  CLOCK,
  input  UI,
  input  STORE,
  input  RESET,
  input  LI,
  input  MOV,
  input  [3:0] ADDRESS,
  input  [7:0] INPUT,
  output [7:0] ACC,
  output [7:0] OUT
);

  wire and_1_out, decoder_1_out0, decoder_1_out1, decoder_1_out2, decoder_1_out3, decoder_1_out4,
       decoder_1_out5, decoder_1_out6, decoder_1_out7, decoder_2_out0, decoder_2_out1, decoder_2_out2,
       decoder_2_out3, decoder_2_out4, decoder_2_out5, decoder_2_out6, decoder_2_out7, not_1_out, undriven;
  wire [7:0] register_2_q, register_3_q, register_4_q, register_5_q, register_6_q, register_7_q,
       register_8_q, register_9_q, register_10_q, register_11_q, register_12_q, register_13_q, register_14_q,
       register_15_q, register_16_q;

  and and_1 (and_1_out, MOV, CLOCK);
  Decoder #(.select(3), .disabled(0)) decoder_1 (
    .out0(decoder_1_out0), .out1(decoder_1_out1), .out2(decoder_1_out2), .out3(decoder_1_out3),
    .out4(decoder_1_out4), .out5(decoder_1_out5), .out6(decoder_1_out6), .out7(decoder_1_out7),
    .sel(ADDRESS[2:0]), .en(not_1_out));
  not not_1 (not_1_out, ADDRESS[3]);
  Decoder #(.select(3), .disabled(0)) decoder_2 (
    .out0(decoder_2_out0), .out1(decoder_2_out1), .out2(decoder_2_out2), .out3(decoder_2_out3),
    .out4(decoder_2_out4), .out5(decoder_2_out5), .out6(decoder_2_out6), .out7(decoder_2_out7),
    .sel(ADDRESS[2:0]), .en(ADDRESS[3]));
  assign INPUT = UI ? {IMM, ACC[3:0]} : 8'bz;  // Controlled_Buffer controlled_buffer_1
  assign INPUT = LI ? {ACC[7:4], IMM} : 8'bz;  // Controlled_Buffer controlled_buffer_2
  Register register_1 (.D(INPUT), .en(STORE), .Q(ACC), .clk(CLOCK), .clr(RESET));
  Register register_2 (.D(INPUT), .en(decoder_1_out1), .Q(register_2_q), .clk(and_1_out));  // open: clr
  Register register_3 (.D(INPUT), .en(decoder_1_out2), .Q(register_3_q), .clk(and_1_out), .clr(undriven));
  Register register_4 (.D(INPUT), .en(decoder_1_out3), .Q(register_4_q), .clk(and_1_out));  // open: clr
  Register register_5 (.D(INPUT), .en(decoder_1_out4), .Q(register_5_q), .clk(and_1_out));  // open: clr
  Register register_6 (.D(INPUT), .en(decoder_1_out5), .Q(register_6_q), .clk(and_1_out));  // open: clr
  Register register_7 (.D(INPUT), .en(decoder_1_out6), .Q(register_7_q), .clk(and_1_out));  // open: clr
  Register register_8 (.D(INPUT), .en(decoder_1_out7), .Q(register_8_q), .clk(and_1_out));  // open: clr
  Register register_9 (.D(INPUT), .en(decoder_2_out0), .Q(register_9_q), .clk(and_1_out));  // open: clr
  Register register_10 (.D(INPUT), .en(decoder_2_out1), .Q(register_10_q), .clk(and_1_out));  // open: clr
  Register register_11 (.D(INPUT), .en(decoder_2_out2), .Q(register_11_q), .clk(and_1_out));  // open: clr
  Register register_12 (.D(INPUT), .en(decoder_2_out3), .Q(register_12_q), .clk(and_1_out));  // open: clr
  Register register_13 (.D(INPUT), .en(decoder_2_out4), .Q(register_13_q), .clk(and_1_out));  // open: clr
  Register register_14 (.D(INPUT), .en(decoder_2_out5), .Q(register_14_q), .clk(and_1_out));  // open: clr
  Register register_15 (.D(INPUT), .en(decoder_2_out6), .Q(register_15_q), .clk(and_1_out));  // open: clr
  Register register_16 (.D(INPUT), .en(decoder_2_out7), .Q(register_16_q), .clk(and_1_out));  // open: clr
  Multiplexer #(.select(3), .width(8)) multiplexer_1 (
    .in0(register_9_q), .in1(register_10_q), .in2(register_11_q), .in3(register_12_q), .in4(register_13_q),
    .in5(register_14_q), .in6(register_15_q), .in7(register_16_q), .out(OUT), .sel(ADDRESS[2:0]),
    .en(ADDRESS[3]));
  Multiplexer #(.select(3), .width(8)) multiplexer_2 (
    .in0(ACC), .in1(register_2_q), .in2(register_3_q), .in3(register_4_q), .in4(register_5_q),
    .in5(register_6_q), .in6(register_7_q), .in7(register_8_q), .out(OUT), .sel(ADDRESS[2:0]), .en(not_1_out));
endmodule

module DISP (
  input  CLOCK,
  input  [7:0] DATA,
  input  [7:0] OTHER,
  input  DISP,
  output [7:0] ROWS,
  output [7:0] COLUMNS,
  output RESET
);

  wire [2:0] register_2_q;
  wire [7:0] register_1_q;

  Register #(.trigger("falling")) register_1 (.D(DATA), .en(DISP), .Q(register_1_q), .clk(CLOCK));  // open: clr
  and u_RESET (RESET, DISP, OTHER[3]);
  Register #(.width(3), .trigger("falling")) register_2 (
    .D(OTHER[2:0]), .en(DISP), .Q(register_2_q), .clk(CLOCK));  // open: clr
  assign ROWS = register_1_q;  // Buffer DRIVER, 8 bits wide
  Decoder #(.select(3), .enable("false")) decoder_1 (
    .out0(COLUMNS[0]), .out1(COLUMNS[1]), .out2(COLUMNS[2]), .out3(COLUMNS[3]), .out4(COLUMNS[4]),
    .out5(COLUMNS[5]), .out6(COLUMNS[6]), .out7(COLUMNS[7]), .sel(register_2_q));
endmodule

module DisplayEmulator (
  input  CLOCK,
  input  [7:0] ROWS,
  input  [7:0] COLUMNS,
  input  RESET,
  output [7:0] _0,
  output [7:0] _1,
  output [7:0] _2,
  output [7:0] _3,
  output [7:0] _4,
  output [7:0] _5,
  output [7:0] _6,
  output [7:0] _7
);

  wire and_1_out;

  and and_1 (and_1_out, ~CLOCK, RESET);  // AND_Gate
  Register register_1 (.D(ROWS), .en(COLUMNS[0]), .Q(_0), .clk(CLOCK), .clr(and_1_out));
  Register register_2 (.D(ROWS), .en(COLUMNS[1]), .Q(_1), .clk(CLOCK), .clr(and_1_out));
  Register register_3 (.D(ROWS), .en(COLUMNS[2]), .Q(_2), .clk(CLOCK), .clr(and_1_out));
  Register register_4 (.D(ROWS), .en(COLUMNS[3]), .Q(_3), .clk(CLOCK), .clr(and_1_out));
  Register register_5 (.D(ROWS), .en(COLUMNS[4]), .Q(_4), .clk(CLOCK), .clr(and_1_out));
  Register register_6 (.D(ROWS), .en(COLUMNS[5]), .Q(_5), .clk(CLOCK), .clr(and_1_out));
  Register register_7 (.D(ROWS), .en(COLUMNS[6]), .Q(_6), .clk(CLOCK), .clr(and_1_out));
  Register register_8 (.D(ROWS), .en(COLUMNS[7]), .Q(_7), .clk(CLOCK), .clr(and_1_out));
endmodule

module Input (
  input  [3:0] SELECT,
  input  CLC,
  input  INPUT,
  input  Button1,
  input  Button2,
  input  Button3,
  input  Button4,
  input  Button5,
  input  Button6,
  output INPUTFLAG
);

  wire multiplexer_1_out;

  Multiplexer #(.select(4)) multiplexer_1 (
    .in0(1'b0), .in1(Button1), .in2(Button2), .in3(Button3), .in4(Button4), .in5(Button5), .in6(Button6),
    .out(multiplexer_1_out), .sel(SELECT), .en(INPUT));  // open: in7, in8, in9, in10, in11, in12, in13, in14, in15
  D_Flip_Flop d_ff_1 (.clk(CLC), .D(multiplexer_1_out), .Q(INPUTFLAG), .en(INPUT));  // open: Qn, preset, reset
endmodule

module Control_Logic (
  input  enabled,
  input  [7:0] instruction,
  output [3:0] immediate,
  output [15:0] opcode
);

  Decoder #(.select(4)) decoder_1 (
    .out0(opcode[0]), .out1(opcode[1]), .out2(opcode[2]), .out3(opcode[3]), .out4(opcode[4]),
    .out5(opcode[5]), .out6(opcode[6]), .out7(opcode[7]), .out8(opcode[8]), .out9(opcode[9]),
    .out10(opcode[10]), .out11(opcode[11]), .out12(opcode[12]), .out13(opcode[13]), .out14(opcode[14]),
    .out15(opcode[15]), .sel(instruction[7:4]), .en(enabled));

  assign immediate = instruction[3:0];
endmodule
